# Fritzing sketch Fritzing Sketch (saved by Fritzing 1.0.4)
breadboards: 1

parts:
  U1 = Arduino Leonardo (Rev3b)
  R1 = Resistor [tolerance=±5% power=0.25W resistance=330 package=THT]
  R2 = Resistor [tolerance=±5% power=0.25W resistance=330 package=THT]
  Activity_LED = smd LED [color="Red (633nm)" package="0603 [SMD]"]
  Power_LED = smd LED [color="Red (633nm)" package="0603 [SMD]"]
  S1 = Taiway 100-SP-X-T1 SPDT Miniature Toggle Switch [part_number=100-SP-X-T1-0-0-B1-M package=THT]

nets:
  N1: U1.D11_PWM, R2.Pin_0
  N2: U1.D12/A11, S1.L2
  N3: U1.D13_PWM, R1.Pin_0
  N4: R1.Pin_1, Activity_LED.anode
  N5: R2.Pin_1, Power_LED.anode
  GND: Activity_LED.cathode, Power_LED.cathode, S1.COM
